# Fritzing sketch circuito (saved by Fritzing 0.9.3b)
breadboards: 1

parts:
  Componente1 = Arduino Mega 2560 (Rev3)
  R2 = Rotary Potentiometer (Small) [maximum_resistance=100kΩ package=THT]
  R3 = Rotary Potentiometer (Small) [maximum_resistance=100kΩ package=THT]
  R4 = Rotary Potentiometer (Small) [maximum_resistance=100kΩ package=THT]
  R5 = Rotary Potentiometer (Small) [maximum_resistance=100kΩ package=THT]
  R6 = Rotary Potentiometer (Small) [maximum_resistance=100kΩ package=THT]
  S1 = SWITCH-MOMENTARY-2 [package=tactile-pth-12mm]

nets:
  N1: Componente1.A15, S1.1
  N2: Componente1.A0, R2.wiper
  N3: Componente1.A1, R3.wiper
  N4: Componente1.A2, R4.wiper
  N5: Componente1.A3, R5.wiper
  N6: Componente1.A4, R6.wiper
  N7: Componente1.5V, R2.leg1, R3.leg1, R4.leg1, R5.leg1, R6.leg1, S1.2
  N8: Componente1.GND, R2.leg2, R3.leg2, R4.leg2, R5.leg2, R6.leg2

notes:
  HM-10
